# Fritzing sketch rgb_led_strip (saved by Fritzing 0.9.3b)
breadboards: 1

parts:
  U1 = Sharp PC817 [package=THT]
  U2 = Sharp PC817 [package=THT]
  U3 = Sharp PC817 [package=THT]
  R1 = Resistor [tolerance=±5% resistance=220 package=THT]
  Componente1 = Arduino Mega 2560 (Rev3)
  J1 = Power Jack [package=power_jack_slot]
  J2 = female pin header, 4 pins [form="♀ (female)"]

nets:
  N1: U1.Pin_1, U2.Pin_1, U3.Pin_1, R1.Pin_0
  N2: U1.Pin_2, Componente1.D8_PWM
  N3: U1.Pin_4, J2.pin2
  N4: U1.Pin_3, U2.Pin_3, U3.Pin_3, J1.GND
  N5: U2.Pin_2, Componente1.D9_PWM
  N6: U2.Pin_4, J2.pin3
  N7: U3.Pin_2, Componente1.D10_PWM
  N8: U3.Pin_4, J2.pin4
  N9: R1.Pin_1, Componente1.5V
  N10: J1.PWR, J2.pin1
